# Fritzing sketch Diagram (saved by Fritzing 0.9.3b)
breadboards: 1

parts:
  U1 = ESP8266 NodeMCU LoLin module
  R1 = Photocell (LDR) [package=THT]
  R2 = Resistor [tolerance=±5% resistance=220 package="0805 [SMD]"]
  R3 = Resistor [tolerance=±5% resistance=220 package="0805 [SMD]"]
  R4 = Photocell (LDR) [package=THT]
  R5 = Photocell (LDR) [package=THT]
  R6 = Resistor [tolerance=±5% resistance=220 package="0805 [SMD]"]
  LED1 = smd LED [color="Red (633nm)" package="0805 [SMD]"]
  R7 = Resistor [tolerance=±5% resistance=220 package="0805 [SMD]"]

nets:
  N1: U1.D1, LED1.anode
  N2: U1.3V3, R1.pin_1, R4.pin_1, R5.pin_1
  N3: U1.GND, R2.Pin_1, R3.Pin_1, R6.Pin_1, LED1.cathode, R7.Pin_0, R7.Pin_1
  N4: U1.A0, R1.pin_0, R2.Pin_0, R3.Pin_0, R4.pin_0, R5.pin_0, R6.Pin_0

custom parts:
  ESP8266 NodeMCU LoLin module: ESP8266 based NodeMCU
